# Fritzing sketch IOTProject (saved by Fritzing 0.9.4)
breadboards: 1

parts:
  Arduino_Mega = Arduino Mega 2560 (Rev3)
  R1 = Resistor [tolerance=±5% resistance=220 package=THT]
  DHT22 = DHT22 Humidity and Temperature Sensor
  MQ135 = GAS_SENSOR [package=mq-3]
  128x32_OLED_Display = OLED Monochrome 128x32 I2C [part_number=931]

nets:
  N1: Arduino_Mega.A0, MQ135.A1
  N2: Arduino_Mega.D21/SCL, 128x32_OLED_Display.SCL
  N3: Arduino_Mega.D20/SDA, 128x32_OLED_Display.SDA
  5V: Arduino_Mega.5V, R1.Pin_0, DHT22.VDD, MQ135.B1, 128x32_OLED_Display.3.3V
  GND: Arduino_Mega.GND, DHT22.GND, 128x32_OLED_Display.GND
  N4: Arduino_Mega.D50, R1.Pin_1, DHT22.DATA

custom parts:
  OLED Monochrome 128x32 I2C: These displays are small, only about 1" diagonal, but very readable due to the high contrast of an OLED display. This display is made of 128x32 individual white OLED pixels, each one is turned on or off by the controller chip. Because the display makes its own light, no backlight is required. This reduces the power required to run the OLED and is why the display has such high contrast; we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
